# Fritzing sketch sketch (saved by Fritzing 0.9.2b)
breadboards: 1

parts:
  Q1 = TRANSISTOR_NPN [package=to-92-ammo]
  R1 = Resistor [tolerance=±5% resistance=330 package="2512 [SMD]"]
  Raspberry_Pi1 = Raspberry Pi 2
  S6 = Momentary Switch [package=ksa_sealed_tac_switch]
  BAT1 = BC9VPC [package=bc9vpc]
  R2 = Resistor [tolerance=±5% resistance=12 package="2010 [SMD]"]
  R3 = Resistor [tolerance=±5% resistance=330 package="2512 [SMD]"]
  Q2 = TRANSISTOR_NPN [package=to-92-ammo]
  R4 = Resistor [tolerance=±5% resistance=12 package="2010 [SMD]"]

nets:
  N1: Q1.E, Raspberry_Pi1.GND, S6.4, BAT1.V-, Q2.E
  N2: Q1.B, R2.Pin_1
  N3: Q1.C, R1.Pin_0
  N4: R1.Pin_1, Raspberry_Pi1.GPIO2
  N5: Raspberry_Pi1.GPIO3, R3.Pin_1
  N6: Raspberry_Pi1.GPIO14, S6.2
  N7: BAT1.V+, R2.Pin_0, R4.Pin_0
  N8: R3.Pin_0, Q2.C
  N9: Q2.B, R4.Pin_1
